# Fritzing sketch Phase2 (saved by Fritzing 0.9.6b)
breadboards: 1

parts:
  R1 = Resistor [tolerance=±0.1% power=0.25 resistance=220 package=THT]
  Orange_GPIO_17_Red_3_3V_Black_Ground = Raspberry Pi 4B
  RHT1 = Humidity and Temperature Sensor RHT03
  LED1 = LED - 5mm [color="Red (633nm)" current=0.030 package="5 mm [THT]"]
  R2 = Resistor [tolerance=±0.1% power=0.25 resistance=220 package=THT]

nets:
  N1: R1.Pin_0, Orange_GPIO_17_Red_3_3V_Black_Ground.GND, RHT1.GND_2
  N2: R1.Pin_1, LED1.anode
  3V3: Orange_GPIO_17_Red_3_3V_Black_Ground.3V3, RHT1.Vcc, R2.Pin_0
  N3: Orange_GPIO_17_Red_3_3V_Black_Ground.GPIO17, RHT1.Data-signal, R2.Pin_1
