# Fritzing sketch Phase3 (saved by Fritzing 0.9.6b)
breadboards: 1

parts:
  J1 = T Cobbler Plus
  LED1 = LED - 3mm [color="Red (633nm)" current=0.030 package="3 mm [THT]"]
  RHT1 = Humidity and Temperature Sensor RHT03
  R4 = Resistor [tolerance=±5% power=0.25 resistance=220 package=THT]
  R5 = Resistor [tolerance=±5% power=0.25 resistance=220 package=THT]

nets:
  N1: J1.GND#8, RHT1.GND_2, R4.Pin_1
  N2: J1.#17, RHT1.GND_1
  N3: J1.#27, LED1.cathode
  3.3V: J1.3.3V, RHT1.Vcc, R5.Pin_0
  N4: LED1.anode, R4.Pin_0
  N5: RHT1.Data-signal, R5.Pin_1

custom parts:
  T Cobbler Plus: The T-Cobbler Plus is an add on prototyping board from Adafruit specifically designed for the Raspberry Pi B+ that can break out all those tasty power, GPIO, I2C and SPI pins from the 40-pin header onto a solderless breadboard. This set will make "cobbling together" prototypes with the Pi super easy. The T-Cobbler Plus can plug into any solderless breadboard.
